# Fritzing sketch Untitled Sketch (saved by Fritzing 0.9.3b)
breadboards: 1

parts:
  WeMos_D1_Mini1 = WeMos D1 Mini
  T1 = LM35 Temperature Sensor [package="TO92 [THT]"]
  U1 = 7-SEGMENT-4DIGIT [package=7-segment-4digit-youngsun]  # not connected
  U5 = 74HC595 [package="DIP16 [THT]"]  # not connected

nets:
  N1: WeMos_D1_Mini1.5V, T1.+Vs
  N2: WeMos_D1_Mini1.A0, T1.Vout
  N3: WeMos_D1_Mini1.G, T1.GND
