# Fritzing sketch 0828 (saved by Fritzing 0.9.3b)
breadboards: 1

parts:
  元件1 = Arduino Uno (Rev3)
  LED1 = LED - 3mm [color="Red (633nm)" package="3 mm [THT]"]
  R1 = Resistor [tolerance=±5% resistance=220 package=THT]
  S1 = Pushbutton [package="[THT]"]
  S3 = Pushbutton [package="[THT]"]
  LED2 = LED - 3mm [color="Yellow (595nm)" package="3 mm [THT]"]
  LED3 = LED - 3mm [color="Green (570nm)" package="3 mm [THT]"]
  R2 = Resistor [tolerance=±5% resistance=220 package=THT]
  R3 = Resistor [tolerance=±5% resistance=220 package=THT]

nets:
  N1: 元件1.D8, R1.Pin_0
  N2: 元件1.D9_PWM, R2.Pin_0
  N3: 元件1.D10_PWM/SS, R3.Pin_0
  N4: 元件1.D2, S3.Pin_3, S3.Pin_4
  N5: 元件1.D4, S1.Pin_3, S1.Pin_4
  N6: 元件1.GND, LED1.cathode, S1.Pin_1, S1.Pin_2, S3.Pin_1, S3.Pin_2, LED2.cathode, LED3.cathode
  N7: LED1.anode, R1.Pin_1
  N8: LED2.anode, R2.Pin_1
  N9: LED3.anode, R3.Pin_1
