# Fritzing sketch mcp3008 (saved by Fritzing 0.9.3b)
breadboards: 1

parts:
  元件1 = Adafruit T-Cobbler Plus [part_number="Adafruit #1989 and #2028"]
  IC1 = MCP3008 8-channel 10-bit ADC [part_number=MCP3008]
  R1 = Rotary Potentiometer (Small) [maximum_resistance=100kΩ package=THT]

nets:
  N1: 元件1.+3.3V, IC1.no_name_yet#15, IC1.no_name_yet#16, R1.leg1
  N2: 元件1.GND, IC1.no_name_yet#9, IC1.no_name_yet#14, R1.leg2
  N3: 元件1.MOSI, IC1.no_name_yet#11
  N4: 元件1.MISO, IC1.no_name_yet#12
  N5: 元件1.SCLK, IC1.no_name_yet#13
  N6: 元件1.CE0, IC1.no_name_yet#10
  N7: IC1.no_name_yet#1, R1.wiper

custom parts:
  Adafruit T-Cobbler Plus: The Raspberry Pi has landed on the Maker World like a 40-GPIO pinned, quad-USB ported, credit card sized bomb of DIY joy. And while you can use most of our great Model B accessories by hooking up our downgrade cable, its probably a good time to upgrade your set up and accessorize using all of the 40 pins. That's why we now carry the Assembled Adafruit Pi T-Cobbler Plus - Breakout + Cable for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
